// Logisim project q02b.circ as structural Verilog: 1 circuit, main circuit main
module main (
  input  a,
  input  b,
  input  c,
  output out_4
);

  wire nand_1_out, nand_2_out, nand_3_out;

  nand nand_1 (nand_1_out, c, c);
  nand nand_2 (nand_2_out, a, nand_1_out);
  nand nand_3 (nand_3_out, a, b);
  nand nand_4 (out_4, nand_2_out, nand_3_out);
endmodule
