// Logisim project q02c.circ as structural Verilog: 1 circuit, main circuit main
module main (
  input  a,
  input  b,
  input  c,
  output out_4
);

  wire not_1_out, or_1_out;

  or or_1 (or_1_out, b, not_1_out);
  not not_1 (not_1_out, c);
  and and_1 (out_4, a, or_1_out);
endmodule
