// Logisim project q02d.circ as structural Verilog: 1 circuit, main circuit main
module main (
  input  a,
  input  b,
  input  c,
  output out_4
);

  wire multiplexer_1_out, multiplexer_2_out, multiplexer_3_out, multiplexer_4_out, not_1_out, not_2_out,
       not_3_out;

  not not_1 (not_1_out, a);
  not not_2 (not_2_out, b);
  not not_3 (not_3_out, c);
  Multiplexer #(.enable("false")) multiplexer_1 (.in0(1'b0), .in1(b), .out(multiplexer_1_out), .sel(a));
  Multiplexer #(.enable("false")) multiplexer_2 (.in0(1'b0), .in1(c), .out(multiplexer_2_out), .sel(multiplexer_1_out));
  Multiplexer #(.enable("false")) multiplexer_3 (.in0(1'b0), .in1(not_2_out), .out(multiplexer_3_out), .sel(not_1_out));
  Multiplexer #(.enable("false")) multiplexer_4 (
    .in0(1'b0), .in1(not_3_out), .out(multiplexer_4_out), .sel(multiplexer_3_out));
  Multiplexer #(.enable("false")) multiplexer_5 (
    .in0(1'b1), .in1(multiplexer_4_out), .out(out_4), .sel(multiplexer_2_out));
endmodule
