// Logisim project q03.circ as structural Verilog: 1 circuit, main circuit main
module main (
  input  a,
  input  b,
  input  c,
  output out_4
);

  wire nand_1_out, nand_2_out, nand_3_out, nand_4_out, nand_5_out;

  nand nand_1 (nand_1_out, a, a);
  nand nand_2 (nand_2_out, b, b);
  nand nand_3 (nand_3_out, c, nand_1_out);
  nand nand_4 (nand_4_out, nand_1_out, b);
  nand nand_5 (nand_5_out, c, nand_2_out);
  nand nand_6 (out_4, nand_3_out, nand_4_out, nand_5_out);
endmodule
