// Logisim project 04.circ as structural Verilog: 1 circuit, main circuit main
module main (
  output out_1,
  output out_2,
  output out_3
);

  wire clock_1_out, not_1_out, not_2_out, not_3_out;

  Clock clock_1 (.out(clock_1_out));
  not not_1 (not_1_out, 1'b1);
  J_K_Flip_Flop j_k_ff_1 (.J(1'b1), .clk(clock_1_out), .K(1'b1), .Q(out_3), .reset(not_1_out));  // open: Qn, preset
  J_K_Flip_Flop j_k_ff_2 (.J(1'b1), .clk(out_3), .K(1'b1), .Q(out_2), .reset(not_2_out));  // open: Qn, preset
  not not_2 (not_2_out, 1'b1);
  J_K_Flip_Flop j_k_ff_3 (.J(1'b1), .clk(out_2), .K(1'b1), .Q(out_1), .reset(not_3_out));  // open: Qn, preset
  not not_3 (not_3_out, 1'b1);
endmodule
