// Logisim project guia0503.circ as structural Verilog: 1 circuit, main circuit main
module main (
  input  a,
  input  b,
  output out_3
);

  wire nand_1_out, nand_2_out;

  nand nand_1 (nand_1_out, b, b);
  nand nand_2 (nand_2_out, a, nand_1_out);
  nand nand_3 (out_3, nand_2_out, nand_2_out);

  // Notes on the sheet:
  //   ~(~a | b) = (a . ~b)
  //   a . ~b
  //   negando com nand
  //   nand(a,b) nand nand(a,b)
endmodule
