// Logisim project guia0505.circ as structural Verilog: 1 circuit, main circuit main
module main (
  input  a,
  input  b,
  output out_3
);

  wire nand_1_out, nand_2_out, nand_3_out, nand_4_out, nand_5_out;

  nand nand_1 (nand_1_out, b, b);
  nand nand_2 (nand_2_out, a, a);
  nand nand_3 (nand_3_out, nand_1_out, a);
  nand nand_4 (nand_4_out, b, nand_2_out);
  nand nand_5 (nand_5_out, nand_3_out, nand_4_out);
  nand nand_6 (out_3, nand_5_out, nand_5_out);

  // Notes on the sheet:
  //   ~(a ^ b) = XNOR(a,b)
  //   XOR = (a & ~b) | (~a & b)
  //   and com NAND
  //   nand(a,a) nand nand(b,b)
endmodule
