// Logisim project guia0605.circ as structural Verilog: 1 circuit, main circuit main
module main (
  input  x,
  input  y,
  input  z,
  output out_4
);

  wire and_1_out, and_2_out, and_3_out, not_1_out, not_2_out, not_3_out, not_4_out, not_5_out, not_6_out,
       or_1_out, or_2_out;

  not not_1 (not_1_out, y);
  not not_2 (not_2_out, x);
  and and_1 (and_1_out, z, y);
  not not_3 (not_3_out, x);
  or or_1 (or_1_out, not_1_out, not_2_out);
  and and_2 (and_2_out, y, x);
  or or_2 (or_2_out, and_1_out, not_3_out);
  not not_4 (not_4_out, or_1_out);
  and and_3 (and_3_out, not_4_out, not_5_out);
  not not_5 (not_5_out, and_2_out);
  not not_6 (not_6_out, or_2_out);
  or or_3 (out_4, and_3_out, not_6_out);
endmodule
