// Logisim project 01.circ as structural Verilog: 1 circuit, main circuit main
module main (
  input  a,
  input  b,
  input  in_3,
  output out_4
);

  wire and_1_out, nand_1_out;

  and and_1 (and_1_out, a, b);
  nand nand_1 (nand_1_out, a, b);
  Multiplexer #(.enable("false")) multiplexer_1 (.in0(and_1_out), .in1(nand_1_out), .out(out_4), .sel(in_3));
endmodule
