// Logisim project 05.circ as structural Verilog: 1 circuit, main circuit main
module main (
  input  a,
  input  b,
  input  in_3,
  input  in_4,
  input  in_5,
  input  in_6,
  input  in_7,
  input  in_8
);

  wire and_1_out, multiplexer_1_out, multiplexer_2_out, multiplexer_3_out, multiplexer_4_out,
       multiplexer_5_out, nand_1_out, nor_1_out, not_1_out, or_1_out, xnor_1_out, xor_1_out;

  or or_1 (or_1_out, a, b);
  nor nor_1 (nor_1_out, a, b);
  xor xor_1 (xor_1_out, a, b);
  and and_1 (and_1_out, a, b);
  nand nand_1 (nand_1_out, a, b);
  xnor xnor_1 (xnor_1_out, a, b);
  Multiplexer #(.enable("false")) multiplexer_1 (.in0(or_1_out), .in1(nor_1_out), .out(multiplexer_1_out), .sel(in_3));
  Multiplexer #(.enable("false")) multiplexer_2 (
    .in0(xor_1_out), .in1(xnor_1_out), .out(multiplexer_2_out), .sel(in_5));
  not not_1 (not_1_out, a);
  Multiplexer #(.enable("false")) multiplexer_3 (
    .in0(and_1_out), .in1(nand_1_out), .out(multiplexer_3_out), .sel(in_8));
  Multiplexer #(.enable("false")) multiplexer_4 (
    .in0(multiplexer_1_out), .in1(multiplexer_2_out), .out(multiplexer_4_out), .sel(in_4));
  Multiplexer #(.enable("false")) multiplexer_5 (
    .in0(not_1_out), .in1(multiplexer_3_out), .out(multiplexer_5_out), .sel(in_7));
  Multiplexer #(.enable("false")) multiplexer_6 (
    .in0(multiplexer_4_out), .in1(multiplexer_5_out), .sel(in_6));  // open: out
endmodule
