// Logisim project 01.circ as structural Verilog: 3 circuits, main circuit halfadder
module main (
  input  carry,
  input  [5:0] y,
  input  [5:0] x,
  output [5:0] out_4
);

  wire fulladder_2_s1, fulladder_4_s1, fulladder_6_s1;

  fulladder fulladder_1 (.carry(fulladder_2_s1), .a(x[5]), .b(y[5]), .s0(out_4[5]));  // open: s1
  fulladder fulladder_2 (.carry(out_4[3]), .a(x[4]), .b(y[4]), .s0(out_4[4]), .s1(fulladder_2_s1));
  fulladder fulladder_3 (.carry(fulladder_4_s1), .a(x[3]), .b(y[3]), .s0(out_4[3]), .s1(out_4[3]));
  fulladder fulladder_4 (.carry(fulladder_4_s1), .a(x[2]), .b(y[2]), .s0(out_4[2]), .s1(fulladder_4_s1));
  fulladder fulladder_5 (.carry(fulladder_6_s1), .a(x[1]), .b(y[1]), .s0(out_4[1]), .s1(fulladder_4_s1));
  fulladder fulladder_6 (.carry(carry), .a(x[0]), .b(y[0]), .s0(out_4[0]), .s1(fulladder_6_s1));
endmodule

module halfadder (
  input  x,
  input  y,
  output s0,
  output s1
);

  xor xor_1 (s0, x, y);
  and and_1 (s1, y, x);
endmodule

module fulladder (
  input  carry,
  input  a,
  input  b,
  output s0,
  output s1
);

  wire and_1_out, halfadder_1_s0, halfadder_1_s1;

  halfadder halfadder_1 (.x(a), .y(b), .s0(halfadder_1_s0), .s1(halfadder_1_s1));
  xor xor_1 (s0, carry, halfadder_1_s0);
  and and_1 (and_1_out, halfadder_1_s0, carry);
  or or_1 (s1, and_1_out, halfadder_1_s1);
endmodule
