// Logisim project complemento2.circ as structural Verilog: 4 circuits, main circuit halfadder
module main (
  input  carry,
  input  [5:0] y,
  input  [5:0] x
);

  wire fulladder_2_s1, fulladder_3_s0, fulladder_4_s1, fulladder_6_s1;

  fulladder fulladder_1 (.carry(fulladder_2_s1), .a(x[5]), .b(y[5]));  // open: s0, s1
  fulladder fulladder_2 (.carry(fulladder_3_s0), .a(x[4]), .b(y[4]), .s1(fulladder_2_s1));  // open: s0
  fulladder fulladder_3 (.carry(fulladder_4_s1), .a(x[3]), .b(y[3]), .s0(fulladder_3_s0), .s1(fulladder_3_s0));
  fulladder fulladder_4 (.carry(fulladder_4_s1), .a(x[2]), .b(y[2]), .s1(fulladder_4_s1));  // open: s0
  fulladder fulladder_5 (.carry(fulladder_6_s1), .a(x[1]), .b(y[1]), .s1(fulladder_4_s1));  // open: s0
  fulladder fulladder_6 (.carry(carry), .a(x[0]), .b(y[0]), .s1(fulladder_6_s1));  // open: s0
endmodule

module halfadder (
  input  x,
  input  y,
  output s0,
  output s1
);

  xor xor_1 (s0, x, y);
  and and_1 (s1, y, x);
endmodule

module fulladder (
  input  carry,
  input  a,
  input  b,
  output s0,
  output s1
);

  wire and_1_out, halfadder_1_s0, halfadder_1_s1;

  halfadder halfadder_1 (.x(a), .y(b), .s0(halfadder_1_s0), .s1(halfadder_1_s1));
  xor xor_1 (s0, carry, halfadder_1_s0);
  and and_1 (and_1_out, halfadder_1_s0, carry);
  or or_1 (s1, and_1_out, halfadder_1_s1);
endmodule

module complemento2 (
  input  in_1,
  input  [5:0] x,
  input  [5:0] y,
  output [5:0] out_4
);

  wire fulladder_1_s1, fulladder_2_s1, fulladder_3_s1, fulladder_4_s1, fulladder_5_s1, not_1_out, not_2_out,
       not_3_out, not_4_out, not_5_out, not_6_out, not_7_out, not_8_out, not_9_out, not_10_out, not_11_out,
       not_12_out;

  not not_1 (not_1_out, x[0]);
  not not_2 (not_2_out, y[0]);
  not not_3 (not_3_out, x[1]);
  not not_4 (not_4_out, y[1]);
  not not_5 (not_5_out, x[2]);
  not not_6 (not_6_out, y[2]);
  not not_7 (not_7_out, x[3]);
  not not_8 (not_8_out, y[3]);
  not not_9 (not_9_out, x[4]);
  not not_10 (not_10_out, y[4]);
  not not_11 (not_11_out, x[5]);
  not not_12 (not_12_out, y[5]);
  fulladder fulladder_1 (.carry(in_1), .a(not_1_out), .b(not_2_out), .s0(out_4[0]), .s1(fulladder_1_s1));
  fulladder fulladder_2 (.carry(fulladder_1_s1), .a(not_3_out), .b(not_4_out), .s0(out_4[1]), .s1(fulladder_2_s1));
  fulladder fulladder_3 (.carry(fulladder_2_s1), .a(not_5_out), .b(not_6_out), .s0(out_4[2]), .s1(fulladder_3_s1));
  fulladder fulladder_4 (.carry(fulladder_3_s1), .a(not_7_out), .b(not_8_out), .s0(out_4[3]), .s1(fulladder_4_s1));
  fulladder fulladder_5 (.carry(fulladder_4_s1), .a(not_9_out), .b(not_10_out), .s0(out_4[4]), .s1(fulladder_5_s1));
  fulladder fulladder_6 (.carry(fulladder_5_s1), .a(not_11_out), .b(not_12_out), .s0(out_4[5]));  // open: s1
endmodule
