// Logisim project desigualdade.circ as structural Verilog: 4 circuits, main circuit halfadder
module main (
  input  carry,
  input  [5:0] y,
  input  [5:0] x
);

  wire fulladder_2_s1, fulladder_3_s0, fulladder_4_s1, fulladder_6_s1;

  fulladder fulladder_1 (.carry(fulladder_2_s1), .a(x[5]), .b(y[5]));  // open: s0, s1
  fulladder fulladder_2 (.carry(fulladder_3_s0), .a(x[4]), .b(y[4]), .s1(fulladder_2_s1));  // open: s0
  fulladder fulladder_3 (.carry(fulladder_4_s1), .a(x[3]), .b(y[3]), .s0(fulladder_3_s0), .s1(fulladder_3_s0));
  fulladder fulladder_4 (.carry(fulladder_4_s1), .a(x[2]), .b(y[2]), .s1(fulladder_4_s1));  // open: s0
  fulladder fulladder_5 (.carry(fulladder_6_s1), .a(x[1]), .b(y[1]), .s1(fulladder_4_s1));  // open: s0
  fulladder fulladder_6 (.carry(carry), .a(x[0]), .b(y[0]), .s1(fulladder_6_s1));  // open: s0
endmodule

module halfadder (
  input  x,
  input  y,
  output s0,
  output s1
);

  xor xor_1 (s0, x, y);
  and and_1 (s1, y, x);
endmodule

module fulladder (
  input  carry,
  input  a,
  input  b,
  output s0,
  output s1
);

  wire and_1_out, halfadder_1_s0, halfadder_1_s1;

  halfadder halfadder_1 (.x(a), .y(b), .s0(halfadder_1_s0), .s1(halfadder_1_s1));
  xor xor_1 (s0, carry, halfadder_1_s0);
  and and_1 (and_1_out, halfadder_1_s0, carry);
  or or_1 (s1, and_1_out, halfadder_1_s1);
endmodule

module desigualdade (
  input  [5:0] x,
  input  [5:0] y,
  output out_3
);

  wire or_1_out, or_2_out, or_3_out, or_4_out, xor_1_out, xor_2_out, xor_3_out, xor_4_out, xor_5_out,
       xor_6_out;

  xor xor_1 (xor_1_out, x[0], y[0]);
  xor xor_2 (xor_2_out, x[1], y[1]);
  xor xor_3 (xor_3_out, x[2], y[2]);
  xor xor_4 (xor_4_out, x[3], y[3]);
  xor xor_5 (xor_5_out, x[4], y[4]);
  xor xor_6 (xor_6_out, x[5], y[5]);
  or or_1 (or_1_out, xor_1_out, xor_2_out);
  or or_2 (or_2_out, xor_3_out, xor_4_out);
  or or_3 (or_3_out, xor_5_out, xor_6_out);
  or or_4 (or_4_out, or_1_out, or_2_out);
  or or_5 (out_3, or_4_out, or_3_out);
endmodule
