// Logisim project igualdade.circ as structural Verilog: 4 circuits, main circuit halfadder
module main (
  input  carry,
  input  [5:0] y,
  input  [5:0] x
);

  wire fulladder_2_s1, fulladder_3_s0, fulladder_4_s1, fulladder_6_s1;

  fulladder fulladder_1 (.carry(fulladder_2_s1), .a(x[5]), .b(y[5]));  // open: s0, s1
  fulladder fulladder_2 (.carry(fulladder_3_s0), .a(x[4]), .b(y[4]), .s1(fulladder_2_s1));  // open: s0
  fulladder fulladder_3 (.carry(fulladder_4_s1), .a(x[3]), .b(y[3]), .s0(fulladder_3_s0), .s1(fulladder_3_s0));
  fulladder fulladder_4 (.carry(fulladder_4_s1), .a(x[2]), .b(y[2]), .s1(fulladder_4_s1));  // open: s0
  fulladder fulladder_5 (.carry(fulladder_6_s1), .a(x[1]), .b(y[1]), .s1(fulladder_4_s1));  // open: s0
  fulladder fulladder_6 (.carry(carry), .a(x[0]), .b(y[0]), .s1(fulladder_6_s1));  // open: s0
endmodule

module halfadder (
  input  x,
  input  y,
  output s0,
  output s1
);

  xor xor_1 (s0, x, y);
  and and_1 (s1, y, x);
endmodule

module fulladder (
  input  carry,
  input  a,
  input  b,
  output s0,
  output s1
);

  wire and_1_out, halfadder_1_s0, halfadder_1_s1;

  halfadder halfadder_1 (.x(a), .y(b), .s0(halfadder_1_s0), .s1(halfadder_1_s1));
  xor xor_1 (s0, carry, halfadder_1_s0);
  and and_1 (and_1_out, halfadder_1_s0, carry);
  or or_1 (s1, and_1_out, halfadder_1_s1);
endmodule

module igualdade (
  input  [5:0] x,
  input  [5:0] y,
  output out_3
);

  wire and_1_out, and_2_out, and_3_out, and_4_out, xnor_1_out, xnor_2_out, xnor_3_out, xnor_4_out,
       xnor_5_out, xnor_6_out;

  xnor xnor_1 (xnor_1_out, x[0], y[0]);
  xnor xnor_2 (xnor_2_out, x[1], y[1]);
  xnor xnor_3 (xnor_3_out, x[2], y[2]);
  xnor xnor_4 (xnor_4_out, x[3], y[3]);
  xnor xnor_5 (xnor_5_out, x[4], y[4]);
  xnor xnor_6 (xnor_6_out, x[5], y[5]);
  and and_1 (and_1_out, xnor_1_out, xnor_2_out);
  and and_2 (and_2_out, xnor_3_out, xnor_4_out);
  and and_3 (and_3_out, xnor_5_out, xnor_6_out);
  and and_4 (and_4_out, and_1_out, and_2_out);
  and and_5 (out_3, and_4_out, and_3_out);
endmodule
