// Logisim project guia1101.circ as structural Verilog: 1 circuit, main circuit main
module main (
  input  x,
  input  Reset,
  output y
);

  wire and_2_out, and_3_out, clock_1_out, or_1_out, q0_q, q0_qn, q1_q;

  Clock clock_1 (.out(clock_1_out));
  D_Flip_Flop q1 (.clk(clock_1_out), .D(or_1_out), .Q(q1_q), .reset(Reset));  // open: Qn, preset
  D_Flip_Flop q0 (.clk(clock_1_out), .D(x), .Q(q0_q), .Qn(q0_qn), .reset(Reset));  // open: preset
  and and_1 (y, q1_q, q0_qn, x);
  and and_2 (and_2_out, q1_q, q0_q);
  and and_3 (and_3_out, q0_q, x);
  or or_1 (or_1_out, and_2_out, and_3_out);
endmodule
