// Logisim project guia1102.circ as structural Verilog: 2 circuits, main circuit main
module main (
  input  x,
  input  Reset,
  output out_3
);

  wire clock_1_out, moore_1_d0, moore_1_d1, moore_1_d2, q0_q, q1_q;

  Clock clock_1 (.out(clock_1_out));
  D_Flip_Flop q2 (.clk(clock_1_out), .D(moore_1_d2), .Q(out_3), .reset(Reset));  // open: Qn, preset
  D_Flip_Flop q1 (.clk(clock_1_out), .D(moore_1_d1), .Q(q1_q), .reset(Reset));  // open: Qn, preset
  D_Flip_Flop q0 (.clk(clock_1_out), .D(moore_1_d0), .Q(q0_q), .reset(Reset));  // open: Qn, preset
  moore moore_1 (.q2(out_3), .q1(q1_q), .q0(q0_q), .x(x), .d2(moore_1_d2), .d1(moore_1_d1), .d0(moore_1_d0));
endmodule

module moore (
  input  q2,
  input  q1,
  input  q0,
  input  x,
  output d2,
  output d1,
  output d0
);

  wire and_2_out, and_3_out, and_4_out, and_5_out, and_6_out, and_7_out, not_1_out, not_2_out;

  and and_1 (d2, q1, not_1_out, x);
  not not_1 (not_1_out, q0);
  and and_2 (and_2_out, q0, x);
  and and_3 (and_3_out, q1, x);
  and and_4 (and_4_out, q1, q0);
  and and_5 (and_5_out, q2, x);
  not not_2 (not_2_out, q1);
  and and_6 (and_6_out, not_2_out, x);
  and and_7 (and_7_out, q0, x);
  or or_1 (d1, and_2_out, and_3_out, and_4_out, and_5_out);
  or or_2 (d0, and_6_out, and_7_out);
endmodule
