// Logisim project mealy.circ as structural Verilog: 3 circuits, main circuit main
module main (
  input  x,
  input  Reset,
  output m2,
  output m1
);

  wire clock_1_out;

  Clock clock_1 (.out(clock_1_out));
  mealy mealy_1 (.clock(clock_1_out), .x(x), .Reset(Reset), .y(m2));
  moore moore_1 (.clock(clock_1_out), .x(x), .Reset(Reset), .out_4(m1));
endmodule

module mealy (
  input  clock,
  input  x,
  input  Reset,
  output y
);

  wire and_2_out, and_3_out, or_1_out, q0_q, q0_qn, q1_q;

  D_Flip_Flop q1 (.clk(clock), .D(or_1_out), .Q(q1_q), .reset(Reset));  // open: Qn, preset
  D_Flip_Flop q0 (.clk(clock), .D(x), .Q(q0_q), .Qn(q0_qn), .reset(Reset));  // open: preset
  and and_1 (y, q1_q, q0_qn, x);
  and and_2 (and_2_out, q1_q, q0_q);
  or or_1 (or_1_out, and_2_out, and_3_out);
  and and_3 (and_3_out, q0_q, x);
endmodule

module moore (
  input  clock,
  input  x,
  input  Reset,
  output out_4
);

  wire moore_1_d0, moore_1_d1, moore_1_d2, q0_q, q1_q;

  D_Flip_Flop q2 (.clk(clock), .D(moore_1_d2), .Q(out_4), .reset(Reset));  // open: Qn, preset
  D_Flip_Flop q1 (.clk(clock), .D(moore_1_d1), .Q(q1_q), .reset(Reset));  // open: Qn, preset
  D_Flip_Flop q0 (.clk(clock), .D(moore_1_d0), .Q(q0_q), .reset(Reset));  // open: Qn, preset
  guia1102_moore moore_1 (.q2(out_4), .q1(q1_q), .q0(q0_q), .x(x), .d2(moore_1_d2), .d1(moore_1_d1), .d0(moore_1_d0));
endmodule
