// Logisim project main.circ as structural Verilog: 2 circuits, main circuit main
module main (
  input  x,
  output y
);

  wire clock_1_out, d_ff_1_q, d_ff_2_q, d_ff_3_q, sub_1_d0, sub_1_d1, sub_1_d2, sub_1_dy;

  Clock clock_1 (.out(clock_1_out));
  D_Flip_Flop d_ff_1 (.clk(clock_1_out), .D(sub_1_d2), .Q(d_ff_1_q));  // open: Qn, preset, reset
  D_Flip_Flop d_ff_2 (.clk(clock_1_out), .D(sub_1_d1), .Q(d_ff_2_q));  // open: Qn, preset, reset
  D_Flip_Flop d_ff_3 (.clk(clock_1_out), .D(sub_1_d0), .Q(d_ff_3_q));  // open: Qn, preset, reset
  D_Flip_Flop d_ff_4 (.clk(clock_1_out), .D(sub_1_dy), .Q(y));  // open: Qn, preset, reset
  sub sub_1 (
    .q2(d_ff_1_q), .q1(d_ff_2_q), .q0(d_ff_3_q), .x(x), .d2(sub_1_d2), .d1(sub_1_d1), .d0(sub_1_d0),
    .dy(sub_1_dy));
endmodule

module sub (
  input  q2,
  input  q1,
  input  q0,
  input  x,
  output d2,
  output d1,
  output d0,
  output dy
);

  wire and_1_out, and_3_out, and_4_out, not_1_out, not_2_out, not_3_out, not_4_out, not_5_out, not_6_out;

  and and_1 (and_1_out, q1, q0, not_1_out);
  not not_1 (not_1_out, x);
  not not_2 (not_2_out, q2);
  not not_3 (not_3_out, q1);
  not not_4 (not_4_out, x);
  not not_5 (not_5_out, q0);
  or or_1 (d0, x, q2);
  and and_2 (dy, q2, not_6_out);
  not not_6 (not_6_out, q0);
  or or_2 (d2, and_1_out, q2);
  and and_3 (and_3_out, not_2_out, not_3_out, q0, not_4_out);
  or or_3 (d1, and_3_out, and_4_out);
  and and_4 (and_4_out, q1, not_5_out, x);
endmodule
