// Logisim project guia1302.circ as structural Verilog: 1 circuit, main circuit main
module main (
  input  Reset,
  output out_2,
  output out_3,
  output out_4,
  output out_5,
  output out_6,
  output out_7
);

  wire clock_1_out, q0_qn;

  Clock clock_1 (.out(clock_1_out));
  J_K_Flip_Flop #(.trigger("falling")) q0 (
    .J(1'b1), .clk(clock_1_out), .K(1'b1), .Q(out_7), .Qn(q0_qn), .reset(Reset));  // open: preset
  J_K_Flip_Flop #(.trigger("falling")) q1 (
    .J(1'b1), .clk(out_7), .K(1'b1), .Q(out_6), .reset(Reset));  // open: Qn, preset
  J_K_Flip_Flop #(.trigger("falling")) q2 (
    .J(1'b1), .clk(out_6), .K(1'b1), .Q(out_5), .reset(Reset));  // open: Qn, preset
  J_K_Flip_Flop #(.trigger("falling")) q3 (
    .J(1'b1), .clk(out_5), .K(1'b1), .Q(out_4), .reset(Reset));  // open: Qn, preset
  J_K_Flip_Flop #(.trigger("falling")) q4 (
    .J(1'b1), .clk(out_4), .K(1'b1), .Q(out_3), .reset(Reset));  // open: Qn, preset
  J_K_Flip_Flop #(.trigger("falling")) q5 (
    .J(1'b1), .clk(out_3), .K(1'b1), .Q(out_2), .reset(Reset));  // open: Qn, preset
endmodule
