// Logisim project guia1303.circ as structural Verilog: 1 circuit, main circuit main
module main (
  output out_1,
  output out_2,
  output out_3,
  output out_4,
  output out_5
);

  wire and_1_out, clock_1_out, q0_qn;

  Clock clock_1 (.out(clock_1_out));
  J_K_Flip_Flop #(.trigger("falling")) q0 (
    .J(1'b1), .clk(clock_1_out), .K(1'b1), .Q(out_5), .Qn(q0_qn), .reset(and_1_out));  // open: preset
  J_K_Flip_Flop #(.trigger("falling")) q1 (
    .J(1'b1), .clk(out_5), .K(1'b1), .Q(out_4), .reset(and_1_out));  // open: Qn, preset
  and and_1 (and_1_out, out_4, out_2);
  J_K_Flip_Flop #(.trigger("falling")) q2 (
    .J(1'b1), .clk(out_4), .K(1'b1), .Q(out_3), .reset(and_1_out));  // open: Qn, preset
  J_K_Flip_Flop #(.trigger("falling")) q3 (
    .J(1'b1), .clk(out_3), .K(1'b1), .Q(out_2), .reset(and_1_out));  // open: Qn, preset
  J_K_Flip_Flop #(.trigger("falling")) q4 (
    .J(1'b1), .clk(out_2), .K(1'b1), .Q(out_1), .reset(and_1_out));  // open: Qn, preset
endmodule
