// Logisim project guia1304.circ as structural Verilog: 1 circuit, main circuit main
module main (
  output out_1,
  output out_2,
  output out_3,
  output out_4,
  output out_5
);

  wire and_1_out, clock_1_out, q0_qn, q1_qn, q2_qn, q3_qn;

  Clock clock_1 (.out(clock_1_out));
  J_K_Flip_Flop #(.trigger("falling")) q0 (
    .J(1'b1), .clk(clock_1_out), .K(1'b1), .Q(out_5), .Qn(q0_qn), .preset(and_1_out));  // open: reset
  J_K_Flip_Flop #(.trigger("falling")) q1 (
    .J(1'b1), .clk(q0_qn), .K(1'b1), .Q(out_4), .Qn(q1_qn), .reset(and_1_out));  // open: preset
  J_K_Flip_Flop #(.trigger("falling")) q2 (
    .J(1'b1), .clk(q1_qn), .K(1'b1), .Q(out_3), .Qn(q2_qn), .reset(and_1_out));  // open: preset
  J_K_Flip_Flop #(.trigger("falling")) q3 (
    .J(1'b1), .clk(q2_qn), .K(1'b1), .Q(out_2), .Qn(q3_qn), .preset(and_1_out));  // open: reset
  J_K_Flip_Flop #(.trigger("falling")) q4 (
    .J(1'b1), .clk(q3_qn), .K(1'b1), .Q(out_1), .reset(and_1_out));  // open: Qn, preset
  and and_1 (and_1_out, out_5, out_4, out_3, out_2, out_1);
endmodule
