// Logisim project guia1305.circ as structural Verilog: 1 circuit, main circuit main
module main (
  input  Reset,
  output out_2,
  output out_3,
  output out_4
);

  wire and_1_out, and_2_out, and_3_out, clock_1_out, not_1_out, or_1_out;

  Clock clock_1 (.out(clock_1_out));
  and and_1 (and_1_out, out_4, out_3);
  T_Flip_Flop t_ff_1 (.clk(clock_1_out), .T(not_1_out), .Q(out_4), .reset(Reset));  // open: Qn, preset
  or or_1 (or_1_out, and_1_out, and_2_out);
  and and_2 (and_2_out, out_3, out_2);
  not not_1 (not_1_out, and_3_out);
  and and_3 (and_3_out, out_3, out_2);
  T_Flip_Flop t_ff_2 (.clk(clock_1_out), .T(out_4), .Q(out_3), .reset(Reset));  // open: Qn, preset
  T_Flip_Flop t_ff_3 (.clk(clock_1_out), .T(or_1_out), .Q(out_2), .reset(Reset));  // open: Qn, preset
endmodule
