// Logisim project 04_LeftShiftTwisted.circ as structural Verilog: 1 circuit, main circuit main
module main (
  input  data,
  input  Clear,
  output out_3,
  output out_4,
  output out_5,
  output out_6,
  output out_7
);

  wire clock_1_out, d_ff_1_qn, or_1_out;

  Clock clock_1 (.out(clock_1_out));
  or or_1 (or_1_out, data, d_ff_1_qn);
  D_Flip_Flop d_ff_1 (.clk(clock_1_out), .D(out_4), .Q(out_3), .Qn(d_ff_1_qn), .reset(Clear));  // open: preset
  D_Flip_Flop d_ff_2 (.clk(clock_1_out), .D(out_5), .Q(out_4), .reset(Clear));  // open: Qn, preset
  D_Flip_Flop d_ff_3 (.clk(clock_1_out), .D(out_6), .Q(out_5), .reset(Clear));  // open: Qn, preset
  D_Flip_Flop d_ff_4 (.clk(clock_1_out), .D(out_7), .Q(out_6), .reset(Clear));  // open: Qn, preset
  D_Flip_Flop d_ff_5 (.clk(clock_1_out), .D(or_1_out), .Q(out_7), .reset(Clear));  // open: Qn, preset
endmodule
