// Logisim project 05_conversor_paralelo_serie.circ as structural Verilog: 1 circuit, main circuit main
module main (
  input  clear,
  input  load,
  input  in_3,
  input  in_4,
  input  in_5,
  input  in_6,
  input  in_7,
  output out_8,
  output out_9,
  output out_10,
  output out_11,
  output out_12
);

  wire and_1_out, and_2_out, and_3_out, and_4_out, and_5_out, clock_1_out, or_1_out, or_2_out, or_3_out,
       or_4_out;

  Clock clock_1 (.out(clock_1_out));
  and and_1 (and_1_out, in_3, load);
  D_Flip_Flop d_ff_1 (.clk(clock_1_out), .D(and_1_out), .Q(out_8), .reset(clear));  // open: Qn, preset
  or or_1 (or_1_out, out_8, and_2_out);
  and and_2 (and_2_out, in_4, load);
  D_Flip_Flop d_ff_2 (.clk(clock_1_out), .D(or_1_out), .Q(out_9), .reset(clear));  // open: Qn, preset
  and and_3 (and_3_out, in_5, load);
  or or_2 (or_2_out, out_9, and_3_out);
  D_Flip_Flop d_ff_3 (.clk(clock_1_out), .D(or_2_out), .Q(out_10), .reset(clear));  // open: Qn, preset
  or or_3 (or_3_out, out_10, and_4_out);
  and and_4 (and_4_out, in_6, load);
  D_Flip_Flop d_ff_4 (.clk(clock_1_out), .D(or_3_out), .Q(out_11), .reset(clear));  // open: Qn, preset
  or or_4 (or_4_out, out_11, and_5_out);
  and and_5 (and_5_out, in_7, load);
  D_Flip_Flop d_ff_5 (.clk(clock_1_out), .D(or_4_out), .Q(out_12), .reset(clear));  // open: Qn, preset
endmodule
