// Logisim project a.circ as structural Verilog: 1 circuit, main circuit main
module main (
  input  a,
  input  b,
  input  c,
  output out_4
);

  wire and_1_out, and_2_out, and_3_out, not_1_out;

  and and_1 (and_1_out, a, not_1_out);
  not not_1 (not_1_out, c);
  and and_2 (and_2_out, a, b);
  and and_3 (and_3_out, b, c);
  or or_1 (out_4, and_1_out, and_2_out, and_3_out);
endmodule
