// Logisim project b.circ as structural Verilog: 1 circuit, main circuit main
module main (
  input  a,
  input  b,
  input  c,
  output out_4
);

  wire xor_1_out;

  xor xor_1 (xor_1_out, a, b);
  and and_1 (out_4, xor_1_out, c);
endmodule
