// Logisim project ROL.circ as structural Verilog: 1 circuit, main circuit main
module main (
  input  Load,
  input  in_2,
  input  in_3,
  input  in_4,
  input  in_5,
  input  in_6,
  input  in_7,
  output out_8,
  output out_9,
  output out_10,
  output out_11,
  output out_12,
  output out_13
);

  wire clock_1_out, multiplexer_1_out, multiplexer_2_out, multiplexer_3_out, multiplexer_4_out,
       multiplexer_5_out, multiplexer_6_out;

  Clock clock_1 (.out(clock_1_out));
  Multiplexer #(.enable("false")) multiplexer_1 (.in0(out_9), .in1(in_2), .out(multiplexer_1_out), .sel(Load));
  D_Flip_Flop d_ff_1 (.clk(clock_1_out), .D(multiplexer_1_out), .Q(out_8));  // open: Qn, preset, reset
  Multiplexer #(.enable("false")) multiplexer_2 (.in0(out_10), .in1(in_3), .out(multiplexer_2_out), .sel(Load));
  D_Flip_Flop d_ff_2 (.clk(clock_1_out), .D(multiplexer_2_out), .Q(out_9));  // open: Qn, preset, reset
  Multiplexer #(.enable("false")) multiplexer_3 (.in0(out_11), .in1(in_4), .out(multiplexer_3_out), .sel(Load));
  D_Flip_Flop d_ff_3 (.clk(clock_1_out), .D(multiplexer_3_out), .Q(out_10));  // open: Qn, preset, reset
  Multiplexer #(.enable("false")) multiplexer_4 (.in0(out_12), .in1(in_5), .out(multiplexer_4_out), .sel(Load));
  D_Flip_Flop d_ff_4 (.clk(clock_1_out), .D(multiplexer_4_out), .Q(out_11));  // open: Qn, preset, reset
  Multiplexer #(.enable("false")) multiplexer_5 (.in0(out_13), .in1(in_6), .out(multiplexer_5_out), .sel(Load));
  D_Flip_Flop d_ff_5 (.clk(clock_1_out), .D(multiplexer_5_out), .Q(out_12));  // open: Qn, preset, reset
  Multiplexer #(.enable("false")) multiplexer_6 (.in0(out_8), .in1(in_7), .out(multiplexer_6_out), .sel(Load));
  D_Flip_Flop d_ff_6 (.clk(clock_1_out), .D(multiplexer_6_out), .Q(out_13));  // open: Qn, preset, reset
endmodule
